// Logisim project fullAdder.circ as structural Verilog: 1 circuit, main circuit main
module main (
  input  A_1,
  input  B_1,
  input  A_2,
  input  B_2,
  input  C_in,
  output S,
  output C,
  output S_O,
  output C_O
);

  wire and_2_out, and_3_out, xor_2_out;

  and and_1 (C, A_1, B_1);
  and and_2 (and_2_out, A_2, B_2);
  xor xor_1 (S, A_1, B_1);
  xor xor_2 (xor_2_out, A_2, B_2);
  and and_3 (and_3_out, xor_2_out, C_in);
  xor xor_3 (S_O, xor_2_out, C_in);
  or or_1 (C_O, and_2_out, and_3_out);

  // Notes on the sheet:
  //   Half Adder Circuit 
  //   Full Adder Circuit
endmodule
